# Fritzing sketch retro-connector-IIc-PCB (saved by Fritzing 0.8.0b)
breadboards: 1

parts:
  J1 = shrouded pin header, 34 pins [form="♂ (shrouded male)"]
  Teensy++ = IC, DIP package, 40 pins [chip_label=Teensy++]

nets:
  N1: J1.pin1, Teensy++.pin26
  N2: J1.pin2, Teensy++.pin25
  N3: J1.pin3, Teensy++.pin24
  N4: J1.pin4, Teensy++.pin23
  N5: J1.pin5, Teensy++.pin22
  N6: J1.pin11, J1.pin12, J1.pin14, Teensy++.pin10
  N7: J1.pin13, Teensy++.pin20
  N8: J1.pin16, Teensy++.pin19
  N9: J1.pin17, Teensy++.pin18
  N10: J1.pin18, Teensy++.pin17
  N11: J1.pin19, Teensy++.pin16
  N12: J1.pin21, Teensy++.pin14
  N13: J1.pin22, Teensy++.pin2
  N14: J1.pin23, Teensy++.pin27
  N15: J1.pin24, Teensy++.pin28
  N16: J1.pin25, Teensy++.pin8
  N17: J1.pin26, Teensy++.pin30
  N18: J1.pin27, Teensy++.pin3
  N19: J1.pin28, Teensy++.pin40
  N20: J1.pin29, Teensy++.pin39
  N21: J1.pin30, Teensy++.pin38
  N22: J1.pin31, Teensy++.pin37
  N23: J1.pin32, Teensy++.pin36
  N24: J1.pin33, Teensy++.pin35
  N25: J1.pin34, Teensy++.pin34

notes:
  RetroConnector
  Apple //c
  rev.3
  1
  34
  2
