# Fritzing sketch Joystick Shield PCB rev2 (saved by Fritzing 0.8.7b)
circuit board: 6.02541cm x 3.44311cm
breadboards: 1

parts:
  Game_Port = IC, DIP package, 16 pins [chip_label=IC]
  Teensy = IC, DIP package, 24 pins [chip_label=IC]
  X1 = DB9 Connector [package=db9]
  100KΩ = Resistor [tolerance=±5% resistance=220 package=THT]
  100KΩ_2 = Resistor [tolerance=±5% resistance=220 package=THT]
  33KΩ = Resistor [tolerance=±5% resistance=220 package=THT]
  33KΩ_2 = Resistor [tolerance=±5% resistance=220 package=THT]
  TRINKET1 = Trinket 5V  # not connected

nets:
  N1: Game_Port.pin1, Teensy.pin24, X1.4
  N2: Game_Port.pin2, Teensy.pin11, X1.8, 33KΩ_2.Pin_1
  N3: Game_Port.pin3, Teensy.pin12, X1.5, 33KΩ.Pin_1
  N4: Game_Port.pin6, Teensy.pin15, X1.1, 100KΩ.Pin_1
  N5: Game_Port.pin8, Teensy.pin1, X1.3, 100KΩ.Pin_0, 100KΩ_2.Pin_0, 33KΩ.Pin_0, 33KΩ_2.Pin_0
  N6: Game_Port.pin10, Teensy.pin16, X1.7, 100KΩ_2.Pin_1

notes:
  1
  16
  9
  rev.1
  Joystick
  RetroConnector

custom parts:
  Trinket 5V: Adafruit Trinket 5V
