# Fritzing sketch serial-keyboard-IIe (saved by Fritzing 0.9.2b)
circuit board: 8.89496cm x 4.79287cm
breadboards: 1

parts:
  CTL+RESET = Pushbutton [package="[THT]"]
  R2 = Resistor [tolerance=±5% resistance=470 package=THT]
  R3 = Resistor [tolerance=±5% resistance=470 package=THT]
  S1 = Pushbutton [package="[THT]"]
  CD74HC4067 = IC, DIP package, 24 pins [chip_label=CD74HC4067]
  CD4051B = IC, DIP package, 16 pins [chip_label=IC]
  TEENSY_2_0 = IC, DIP package, 24 pins [chip_label=IC]
  J17 = double row female pin header, 26 pins [form="♀ (female)"]
  J18 = double row female pin header, 26 pins [form="♀ (female)"]

nets:
  N1: CTL+RESET.Pin_1, CTL+RESET.Pin_2, CD4051B.pin6, CD4051B.pin7, CD4051B.pin8, TEENSY_2_0.pin1
  N2: CTL+RESET.Pin_3, CTL+RESET.Pin_4, TEENSY_2_0.pin12, J17.pin8, J18.pin8
  N3: R2.Pin_0, S1.Pin_1, S1.Pin_2, TEENSY_2_0.pin11, J17.pin4, J18.pin4
  N4: R2.Pin_1, R3.Pin_1, CD74HC4067.pin12, J17.pin7, J18.pin7
  N5: R3.Pin_0, J17.pin3, J18.pin3
  N6: S1.Pin_3, S1.Pin_4, CD74HC4067.pin24, CD4051B.pin16, J17.pin2, J18.pin2
  N7: CD74HC4067.pin1, CD4051B.pin3
  N8: CD74HC4067.pin2, J17.pin13, J18.pin13
  N9: CD74HC4067.pin3, J17.pin12, J18.pin12
  N10: CD74HC4067.pin4, J17.pin22, J18.pin22
  N11: CD74HC4067.pin5, J17.pin23, J18.pin23
  N12: CD74HC4067.pin6, J17.pin24, J18.pin24
  N13: CD74HC4067.pin7, J17.pin25, J18.pin25
  N14: CD74HC4067.pin8, J17.pin26, J18.pin26
  N15: CD74HC4067.pin9, J17.pin1, J18.pin1
  N16: CD74HC4067.pin10, TEENSY_2_0.pin5
  N17: CD74HC4067.pin11, TEENSY_2_0.pin6
  N18: CD74HC4067.pin13, TEENSY_2_0.pin3
  N19: CD74HC4067.pin14, TEENSY_2_0.pin4
  N20: CD74HC4067.pin15, TEENSY_2_0.pin2
  N21: CD74HC4067.pin22, J17.pin16, J18.pin16
  N22: CD74HC4067.pin23, J17.pin21, J18.pin21
  N23: CD4051B.pin1, J17.pin11, J18.pin11
  N24: CD4051B.pin2, J17.pin14, J18.pin14
  N25: CD4051B.pin4, J17.pin9, J18.pin9
  N26: CD4051B.pin5, J17.pin10, J18.pin10
  N27: CD4051B.pin9, TEENSY_2_0.pin9
  N28: CD4051B.pin10, TEENSY_2_0.pin8
  N29: CD4051B.pin11, TEENSY_2_0.pin7
  N30: CD4051B.pin12, J17.pin17, J18.pin17
  N31: CD4051B.pin13, J17.pin20, J18.pin20
  N32: CD4051B.pin14, J17.pin18, J18.pin18
  N33: CD4051B.pin15, J17.pin19, J18.pin19
  N34: TEENSY_2_0.pin16, J17.pin15, J18.pin15
  N35: J17.pin5, J18.pin5
  N36: J17.pin6, J18.pin6

notes:
  rev.2
  Serial Keyboard Interface //e
  RetroConnector™
  ‹‹ keyboard
